# Fritzing sketch Motor Driver v0.2 (saved by Fritzing 0.8.7b)
circuit board: 4cm x 3.5cm
breadboards: 1

parts:
  1k = Resistor [tolerance=±5% resistance=1k package=THT]
  1N4001 = Rectifier Diode [part_number=1N4001 package="300 mil [THT]"]
  0_1uF = Electrolytic Capacitor [capacitance=0.1µF package="100 mil [THT, electrolytic]"]
  1k_2 = Resistor [tolerance=±5% resistance=1k package=THT]
  PN2222 = NPN-Transistor [package="TO92 [THT]"]
  1N4001_2 = Rectifier Diode [part_number=1N4001 package="300 mil [THT]"]
  0_1uF_2 = Electrolytic Capacitor [capacitance=0.1µF package="100 mil [THT, electrolytic]"]
  1k_3 = Resistor [tolerance=±5% resistance=1k package=THT]
  PN2222_2 = NPN-Transistor [package="TO92 [THT]"]
  1N4001_3 = Rectifier Diode [part_number=1N4001 package="300 mil [THT]"]
  0_1uF_3 = Electrolytic Capacitor [capacitance=1µF package="100 mil [THT, electrolytic]"]
  PN2222_3 = NPN-Transistor [package="TO92 [THT]"]
  2_(3_3V) = female pin header, 1 pin [form="♀ (female)"]
  1+ = female pin header, 1 pin [form="♀ (female)"]
  2+ = female pin header, 1 pin [form="♀ (female)"]
  3+ = female pin header, 1 pin [form="♀ (female)"]
  1- = female pin header, 1 pin [form="♀ (female)"]
  2- = female pin header, 1 pin [form="♀ (female)"]
  3- = female pin header, 1 pin [form="♀ (female)"]
  3V = female pin header, 1 pin [form="♀ (female)"]
  GND = female pin header, 1 pin [form="♀ (female)"]
  3_(3_3V) = female pin header, 1 pin [form="♀ (female)"]
  1_(3_3V) = female pin header, 1 pin [form="♀ (female)"]

nets:
  N1: 1k.Pin_0, 1_(3_3V).pin1
  N2: 1k.Pin_1, PN2222_3.B
  N3: 1N4001.cathode, 0_1uF.+, 1N4001_2.cathode, 0_1uF_2.+, 1N4001_3.cathode, 0_1uF_3.+, 1+.pin1, 2+.pin1, 3+.pin1, 3V.pin1
  N4: 1N4001.anode, 0_1uF.-, PN2222_3.C, 1-.pin1
  N5: 1k_2.Pin_0, 2_(3_3V).pin1
  N6: 1k_2.Pin_1, PN2222.B
  N7: PN2222.E, PN2222_2.E, PN2222_3.E, GND.pin1
  N8: PN2222.C, 1N4001_2.anode, 0_1uF_2.-, 2-.pin1
  N9: 1k_3.Pin_0, 3_(3_3V).pin1
  N10: 1k_3.Pin_1, PN2222_2.B
  N11: PN2222_2.C, 1N4001_3.anode, 0_1uF_3.-, 3-.pin1
